# Fritzing sketch 7 Touch Boards (saved by Fritzing 0.9.1b)

parts:
  Part1 = Bare Conductive Touch Board
  Part2 = Bare Conductive Touch Board
  Part3 = Bare Conductive Touch Board
  Part4 = Bare Conductive Touch Board
  Part5 = Bare Conductive Touch Board
  Part6 = Bare Conductive Touch Board
  Part7 = Bare Conductive Touch Board

nets:
  N1: Part1.D1/TX, Part2.D1/TX, Part3.D1/TX, Part4.D1/TX, Part5.D1/TX, Part6.D1/TX, Part7.D0/RX
  5V: Part1.5V, Part2.5V, Part6.5V
  GND: Part1.GND, Part2.GND, Part3.GND, Part4.GND, Part5.GND, Part6.GND, Part7.GND
  N2: Part1.A0, Part7.A4
  N3: Part2.A0, Part7.A3
  5V_2: Part3.5V, Part4.5V, Part5.5V, Part7.5V
  N4: Part3.A0, Part7.A0
  N5: Part4.A0, Part7.A1
  N6: Part5.A0, Part7.A2
  N7: Part6.A0, Part7.A5
